// Logisim project 16bit-and.circ as structural Verilog: 1 circuit, main circuit main
module main (
  input  [15:0] A,
  input  [15:0] B,
  output [15:0] Output
);

  _8bit_and_main main_1 (.A(A[7:0]), .B(B[7:0]), .Output(Output[7:0]));
  _8bit_and_main main_2 (.A(A[15:8]), .B(B[15:8]), .Output(Output[15:8]));
endmodule
