// Logisim project 16bit-or.circ as structural Verilog: 1 circuit, main circuit main
module main (
  input  [15:0] A,
  input  [15:0] B,
  output [15:0] Output
);

  assign Output = A | B;  // OR_Gate or_1, 16 bits wide
endmodule
