// Logisim project 16bit-sll.circ as structural Verilog: 1 circuit, main circuit main
module main (
  input  [15:0] in_1,
  input  [3:0] in_2,
  output [15:0] out_3
);

  Shifter #(.width(16)) shifter_1 (.in(in_1), .\dist (in_2), .out(out_3));
endmodule
