// Logisim project 16bit-slt.circ as structural Verilog: 1 circuit, main circuit main
module main (
  input  [15:0] A,
  input  [15:0] B,
  output [15:0] Output
);

  wire comparator_1_lt;

  Comparator #(.width(16)) comparator_1 (.a(A), .b(B), .lt(comparator_1_lt));  // open: gt, eq
  assign Output = {{15{1'b0}}, comparator_1_lt};  // Bit_Extender bit_extender_1
endmodule
