// Logisim project 16bitadder.circ as structural Verilog: 1 circuit, main circuit main
module main (
  input  in_1,
  input  [15:0] in_2,
  input  [15:0] in_3,
  output [15:0] out_4,
  output out_5
);

  wire main_1_cout;

  _8bitadder_main main_1 (.Cin(in_1), .A(in_2[7:0]), .B(in_3[7:0]), .S(out_4[7:0]), .Cout(main_1_cout));
  _8bitadder_main main_2 (.Cin(main_1_cout), .A(in_2[15:8]), .B(in_3[15:8]), .S(out_4[15:8]), .Cout(out_5));
endmodule
