// Logisim project 16bitmultiplier.circ as structural Verilog: 1 circuit, main circuit main
module main (
  input  [15:0] Cin,
  input  [15:0] A,
  input  [15:0] B,
  input  EN,
  input  Reset,
  output [15:0] LO,
  output [15:0] HI
);

  wire [15:0] multiplier_1_cout, multiplier_1_out;

  Multiplier #(.width(16)) multiplier_1 (.a(A), .b(B), .out(multiplier_1_out), .cin(Cin), .cout(multiplier_1_cout));
  Register #(.width(16), .trigger("high")) u_LO (.D(multiplier_1_out), .en(EN), .Q(LO), .clk(1'b1), .clr(Reset));
  Register #(.width(16), .trigger("high")) u_HI (.D(multiplier_1_cout), .en(EN), .Q(HI), .clk(1'b1), .clr(Reset));
endmodule
