// Logisim project 16bitsubtractor.circ as structural Verilog: 1 circuit, main circuit main
module main (
  input  [15:0] Y,
  input  [15:0] X,
  input  Bin,
  output Bout,
  output [15:0] Diff
);

  wire main_2_bout;

  _8bitsubtractor_main main_1 (.Y(Y[15:8]), .X(X[15:8]), .Bout(Bout), .Diff(Diff[15:8]), .Bin(main_2_bout));
  _8bitsubtractor_main main_2 (.Y(Y[7:0]), .X(X[7:0]), .Bout(main_2_bout), .Diff(Diff[7:0]), .Bin(Bin));
endmodule
