// Logisim project 1bitsubtractor.circ as structural Verilog: 1 circuit, main circuit main
module main (
  input  X,
  input  Y,
  input  Bin,
  output Diff,
  output Bout
);

  wire and_1_out, and_2_out, not_1_out, not_2_out, xor_1_out;

  not not_1 (not_1_out, X);
  xor xor_1 (xor_1_out, X, Y);
  and and_1 (and_1_out, not_1_out, Y);
  not not_2 (not_2_out, xor_1_out);
  xor xor_2 (Diff, xor_1_out, Bin);
  and and_2 (and_2_out, Bin, not_2_out);
  or or_1 (Bout, and_2_out, and_1_out);
endmodule
