// Logisim project 2bitadder.circ as structural Verilog: 1 circuit, main circuit main
module main (
  input  Cin,
  input  [1:0] A,
  input  [1:0] B,
  output [1:0] S,
  output Cout
);

  wire main_1_cout;

  _1bitadder_main main_1 (.A(A[0]), .B(B[0]), .C(Cin), .S(S[0]), .Cout(main_1_cout));
  _1bitadder_main main_2 (.A(A[1]), .B(B[1]), .C(main_1_cout), .S(S[1]), .Cout(Cout));
endmodule
