// Logisim project 2bitsubtractor.circ as structural Verilog: 1 circuit, main circuit main
module main (
  input  Bin,
  input  [1:0] Y,
  input  [1:0] X,
  output Bout,
  output [1:0] Diff
);

  wire main_2_bout;

  _1bitsubtractor_main main_1 (.X(X[1]), .Y(Y[1]), .Bin(main_2_bout), .Diff(Diff[1]), .Bout(Bout));
  _1bitsubtractor_main main_2 (.X(X[0]), .Y(Y[0]), .Bin(Bin), .Diff(Diff[0]), .Bout(main_2_bout));
endmodule
