// Logisim project 4bit-and.circ as structural Verilog: 1 circuit, main circuit main
module main (
  input  [3:0] A,
  input  [3:0] B,
  output [3:0] Output
);

  _2bit_and_main main_1 (.A(A[1:0]), .B(B[1:0]), .Output(Output[1:0]));
  _2bit_and_main main_2 (.A(A[3:2]), .B(B[3:2]), .Output(Output[3:2]));
endmodule
