// Logisim project 4bitadder.circ as structural Verilog: 1 circuit, main circuit main
module main (
  input  Cin,
  input  [3:0] A,
  input  [3:0] B,
  output [3:0] S,
  output Cout
);

  wire main_1_cout;

  _2bitadder_main main_1 (.A(A[1:0]), .B(B[1:0]), .S(S[1:0]), .Cout(main_1_cout), .Cin(Cin));
  _2bitadder_main main_2 (.A(A[3:2]), .B(B[3:2]), .S(S[3:2]), .Cout(Cout), .Cin(main_1_cout));
endmodule
