// Logisim project 4bitsubtractor.circ as structural Verilog: 1 circuit, main circuit main
module main (
  input  [3:0] Y,
  input  [3:0] X,
  input  Bin,
  output Bout,
  output [3:0] out_5
);

  wire main_2_bout;

  _2bitsubtractor_main main_1 (.Y(Y[3:2]), .Bin(main_2_bout), .X(X[3:2]), .Bout(Bout), .Diff(out_5[3:2]));
  _2bitsubtractor_main main_2 (.Y(Y[1:0]), .Bin(Bin), .X(X[1:0]), .Bout(main_2_bout), .Diff(out_5[1:0]));
endmodule
