// Logisim project 8bit-and.circ as structural Verilog: 1 circuit, main circuit main
module main (
  input  [7:0] A,
  input  [7:0] B,
  output [7:0] Output
);

  _4bit_and_main main_1 (.A(A[7:4]), .B(B[7:4]), .Output(Output[7:4]));
  _4bit_and_main main_2 (.A(A[3:0]), .B(B[3:0]), .Output(Output[3:0]));
endmodule
