// Logisim project 8bitadder.circ as structural Verilog: 1 circuit, main circuit main
module main (
  input  Cin,
  input  [7:0] A,
  input  [7:0] B,
  output [7:0] S,
  output Cout
);

  wire main_1_cout;

  _4bitadder_main main_1 (.Cin(Cin), .A(A[3:0]), .B(B[3:0]), .S(S[3:0]), .Cout(main_1_cout));
  _4bitadder_main main_2 (.Cin(main_1_cout), .A(A[7:4]), .B(B[7:4]), .S(S[7:4]), .Cout(Cout));
endmodule
