// Logisim project 8bitsubtractor.circ as structural Verilog: 1 circuit, main circuit main
module main (
  input  [7:0] Y,
  input  [7:0] X,
  input  Bin,
  output [7:0] Diff,
  output Bout
);

  wire main_2_bout;

  _4bitsubtractor_main main_1 (.Y(Y[7:4]), .X(X[7:4]), .Bin(main_2_bout), .Bout(Bout), .out_5(Diff[7:4]));
  _4bitsubtractor_main main_2 (.Y(Y[3:0]), .X(X[3:0]), .Bin(Bin), .Bout(main_2_bout), .out_5(Diff[3:0]));
endmodule
