// Logisim project ALU.circ as structural Verilog: 2 circuits, main circuit main
module main (
  input  [15:0] Read_Data_1,
  input  Reset,
  input  [15:0] ALU2,
  input  [3:0] shamt,
  input  [5:0] ALUOp,
  output Overflow,
  output [15:0] Output,
  output Zero,
  output Negative
);

  wire AddOvf, alu_select_1_mult, comparator_1_eq, comparator_2_lt, not_1_out, SubOvf;
  wire [3:0] Select;
  wire [15:0] and_1_out, main_1_diff, main_2_hi, main_2_lo, main_3_out_3, main_4_output, main_5_out_4,
       or_1_out;

  _16bitsubtractor_main main_1 (.Bout(SubOvf), .Bin(1'b0), .Y(ALU2), .X(Read_Data_1), .Diff(main_1_diff));
  _16bitmultiplier_main main_2 (
    .Cin({16{1'b0}}), .A(Read_Data_1), .B(ALU2), .HI(main_2_hi), .LO(main_2_lo), .EN(alu_select_1_mult),
    .Reset(Reset));
  _16bit_sll_main main_3 (.in_1(Read_Data_1), .in_2(shamt), .out_3(main_3_out_3));
  _16bit_slt_main main_4 (.A(Read_Data_1), .B(ALU2), .Output(main_4_output));
  _16bitadder_main main_5 (.in_1(1'b0), .in_2(Read_Data_1), .in_3(ALU2), .out_4(main_5_out_4), .out_5(AddOvf));
  assign and_1_out = Read_Data_1 & ALU2;  // AND_Gate and_1, 16 bits wide
  assign or_1_out = Read_Data_1 | ALU2;  // OR_Gate or_1, 16 bits wide
  ALU_Select alu_select_1 (
    .a(ALUOp[5]), .b(ALUOp[4]), .O1(Select[3]), .c(ALUOp[3]), .d(ALUOp[2]), .e(ALUOp[1]), .f(ALUOp[0]),
    .O2(Select[2]), .O3(Select[1]), .O4(Select[0]), .mult(alu_select_1_mult));
  Multiplexer #(.select(4), .width(16), .enable("false")) multiplexer_1 (
    .in0({16{1'b0}}), .in1(main_5_out_4), .in2(main_1_diff), .in3({16{1'b0}}), .in4(and_1_out),
    .in5(or_1_out), .in6(main_3_out_3), .in7(main_4_output), .in8(main_2_hi), .in9(main_2_lo),
    .in10({16{1'b0}}), .in11({16{1'b0}}), .in12({16{1'b0}}), .in13({16{1'b0}}), .in14({16{1'b0}}),
    .in15({16{1'b0}}), .out(Output), .sel(Select));
  Comparator #(.width(4)) comparator_1 (.a(Select), .b(4'b1001), .eq(comparator_1_eq));  // open: gt, lt
  Comparator #(.width(16)) comparator_2 (.a(Output), .b({16{1'b0}}), .eq(Zero), .lt(comparator_2_lt));  // open: gt
  not not_1 (not_1_out, comparator_1_eq);
  and and_2 (Negative, comparator_2_lt, not_1_out);
  Multiplexer #(.select(4), .enable("false")) multiplexer_2 (
    .in0(1'b0), .in1(AddOvf), .in2(SubOvf), .in3(1'b0), .in4(1'b0), .in5(1'b0), .in6(1'b0), .in7(1'b0),
    .in8(1'b0), .in9(1'b0), .in10(1'b0), .in11(1'b0), .in12(1'b0), .in13(1'b0), .in14(1'b0), .in15(1'b0),
    .out(Overflow), .sel(Select));
endmodule

module ALU_Select (
  input  a,
  input  b,
  input  c,
  input  d,
  input  e,
  input  f,
  output O1,
  output O2,
  output O3,
  output O4,
  output mult
);

  wire and_1_out, and_2_out, and_3_out, and_4_out, and_5_out, and_6_out, and_7_out, and_8_out, and_9_out,
       and_10_out, and_11_out, and_12_out, and_13_out, and_14_out, and_15_out, and_16_out, and_17_out,
       and_18_out, and_19_out, not_1_out, not_2_out, not_3_out, not_4_out, not_5_out, not_6_out, not_7_out,
       not_8_out, not_9_out, not_10_out, not_11_out, not_12_out, not_13_out, not_14_out, not_15_out,
       not_16_out, not_17_out, not_18_out, not_19_out, not_20_out, not_21_out, not_22_out, not_23_out,
       not_24_out, not_25_out, not_26_out, not_27_out, not_28_out, not_29_out, not_30_out;

  not not_1 (not_1_out, c);
  not not_2 (not_2_out, a);
  not not_3 (not_3_out, e);
  not not_4 (not_4_out, f);
  not not_5 (not_5_out, a);
  not not_6 (not_6_out, b);
  not not_7 (not_7_out, c);
  not not_8 (not_8_out, d);
  not not_9 (not_9_out, e);
  not not_10 (not_10_out, f);
  not not_11 (not_11_out, e);
  not not_12 (not_12_out, a);
  not not_13 (not_13_out, b);
  not not_14 (not_14_out, c);
  not not_15 (not_15_out, e);
  not not_16 (not_16_out, a);
  not not_17 (not_17_out, b);
  not not_18 (not_18_out, c);
  not not_19 (not_19_out, d);
  not not_20 (not_20_out, e);
  not not_21 (not_21_out, f);
  not not_22 (not_22_out, b);
  not not_23 (not_23_out, d);
  not not_24 (not_24_out, c);
  not not_25 (not_25_out, d);
  not not_26 (not_26_out, e);
  not not_27 (not_27_out, a);
  not not_28 (not_28_out, d);
  not not_29 (not_29_out, e);
  not not_30 (not_30_out, f);
  and and_1 (and_1_out, b, not_1_out);
  and and_2 (and_2_out, not_2_out, b, d);
  and and_3 (and_3_out, b, d, not_3_out);
  and and_4 (and_4_out, b, d, not_4_out);
  and and_5 (and_5_out, not_5_out, not_6_out, not_7_out, not_8_out, not_9_out);
  and and_6 (and_6_out, c, e, not_10_out);
  and and_7 (and_7_out, a, d, not_11_out);
  and and_8 (and_8_out, not_12_out, not_13_out, not_14_out, not_15_out);
  and and_9 (and_9_out, not_16_out, d, e);
  and and_10 (and_10_out, not_17_out, d, e);
  and and_11 (and_11_out, not_18_out, d, e);
  and and_12 (and_12_out, b, c, not_19_out);
  and and_13 (and_13_out, b, c, not_20_out);
  and and_14 (and_14_out, a, e, not_21_out);
  and and_15 (and_15_out, not_22_out, f);
  and and_16 (and_16_out, c, not_23_out);
  and and_17 (and_17_out, b, not_24_out, e);
  and and_18 (and_18_out, a, not_25_out, not_26_out);
  and and_19 (and_19_out, a, e, f);
  and and_20 (mult, not_27_out, b, c, not_28_out, not_29_out, not_30_out);
  or or_1 (O1, and_1_out, and_2_out, and_3_out, and_4_out);
  or or_2 (O2, and_5_out, and_6_out, and_7_out);
  or or_3 (O3, and_8_out, and_9_out, and_10_out, and_11_out, and_12_out, and_13_out, and_14_out);
  or or_4 (O4, and_15_out, and_16_out, and_17_out, and_18_out, and_19_out);
endmodule
