// Logisim project CPU.circ as structural Verilog: 2 circuits, main circuit main
module main (
  input  CLR,
  input  Reset
);

  wire and_1_out, and_2_out, CLK_out, comparator_1_eq, control_unit_1_alusrc, control_unit_1_branch,
       control_unit_1_regwrite, Jump, main_2_negative, main_2_zero, MemRead, MemToReg, MemWrite, or_1_out,
       RegDst;
  wire [2:0] multiplexer_1_out;
  wire [3:0] adder_1_out_2;
  wire [5:0] ALUOp;
  wire [15:0] ALU, main_1_read_data_1, main_1_read_data_2, main_2_output, main_3_read_data,
       multiplexer_2_out, multiplexer_4_out;
  wire [25:16] n32_1_out;
  wire [27:0] adder_1_out, bit_extender_1_out;
  wire [31:0] adder_2_out, BranchAddr, multiplexer_3_out, multiplexer_5_out, pc_1_pcout;

  PC pc_1 (.PCin(multiplexer_5_out), .PCout(pc_1_pcout), .CLK(CLK_out), .Reset(Reset));
  Adder #(.width(32)) adder_1 (.a(32'h1), .b(pc_1_pcout), .out({adder_1_out_2, adder_1_out}));  // open: cin, cout
  _32 u_32_1 (.Address(pc_1_pcout), .Out({ALUOp, n32_1_out, ALU}));
  Clock CLK (.out(CLK_out));
  assign bit_extender_1_out = {{2{1'b0}}, {n32_1_out, ALU}};  // Bit_Extender bit_extender_1
  Control_Unit control_unit_1 (
    .opcode1(ALUOp[5]), .opcode2(ALUOp[4]), .jump(Jump), .opcode3(ALUOp[3]), .opcode4(ALUOp[2]),
    .branch(control_unit_1_branch), .opcode5(ALUOp[1]), .opcode6(ALUOp[0]), .memread(MemRead),
    .memtoreg(MemToReg), .memwrite(MemWrite), .alusrc(control_unit_1_alusrc),
    .regwrite(control_unit_1_regwrite), .regdst(RegDst));
  assign BranchAddr = {{16{1'b0}}, ALU};  // Bit_Extender bit_extender_2
  RegFile_main main_1 (
    .Write_Data(multiplexer_4_out), .RegWrite(control_unit_1_regwrite), .Read_Data_1(main_1_read_data_1),
    .Read_Data_2(main_1_read_data_2), .WriteAddr(multiplexer_1_out), .CLK(CLK_out),
    .Read_Addr_2(n32_1_out[18:16]), .Read_Addr_1(n32_1_out[23:21]), .Reset(Reset));
  Multiplexer #(.width(3), .enable("false")) multiplexer_1 (
    .in0(n32_1_out[18:16]), .in1(ALU[13:11]), .out(multiplexer_1_out), .sel(RegDst));
  ALU_main main_2 (
    .Read_Data_1(main_1_read_data_1), .ALU2(multiplexer_2_out), .Output(main_2_output), .Zero(main_2_zero),
    .Negative(main_2_negative), .shamt(ALU[9:6]), .ALUOp(ALUOp), .Reset(Reset));  // open: Overflow
  Multiplexer #(.width(16), .enable("false")) multiplexer_2 (
    .in0(ALU), .in1(main_1_read_data_2), .out(multiplexer_2_out), .sel(control_unit_1_alusrc));
  Adder #(.width(32)) adder_2 (.a({adder_1_out_2, adder_1_out}), .b(BranchAddr), .out(adder_2_out));  // open: cin, cout
  Comparator #(.width(6)) comparator_1 (.a(ALUOp), .b(6'b000110), .eq(comparator_1_eq));  // open: gt, lt
  datamemory_main main_3 (
    .Write_Data(main_1_read_data_2), .Address(main_2_output), .Read_Data(main_3_read_data),
    .MemWrite(MemWrite), .CLR(CLR), .MemRead(MemRead), .CLK(CLK_out));
  and and_1 (and_1_out, control_unit_1_branch, main_2_zero);
  and and_2 (and_2_out, control_unit_1_branch, main_2_negative, comparator_1_eq);
  Multiplexer #(.width(32), .enable("false")) multiplexer_3 (
    .in0({adder_1_out_2, adder_1_out}), .in1(adder_2_out), .out(multiplexer_3_out), .sel(or_1_out));
  or or_1 (or_1_out, and_1_out, and_2_out);
  Multiplexer #(.width(16), .enable("false")) multiplexer_4 (
    .in0(main_2_output), .in1(main_3_read_data), .out(multiplexer_4_out), .sel(MemToReg));
  Multiplexer #(.width(32), .enable("false")) multiplexer_5 (
    .in0(multiplexer_3_out), .in1({adder_1_out_2, bit_extender_1_out}), .out(multiplexer_5_out), .sel(Jump));

  // Other names for the same wires on the sheet: shamt[3:0] = ALU[9:6]
endmodule

module PC (
  input  [31:0] PCin,
  input  CLK,
  input  Reset,
  output [31:0] PCout
);

  Register #(.width(32)) register_1 (.D(PCin), .Q(PCout), .clk(CLK), .clr(Reset));  // open: en
endmodule
