// Logisim project ControlUnit.circ as structural Verilog: 1 circuit, main circuit Control Unit
module Control_Unit (
  input  opcode1,
  input  opcode2,
  input  opcode3,
  input  opcode4,
  input  opcode5,
  input  opcode6,
  output jump,
  output branch,
  output memread,
  output memtoreg,
  output memwrite,
  output alusrc,
  output regwrite,
  output regdst
);

  wire and_3_out, and_4_out, and_5_out, and_6_out, and_7_out, and_8_out, and_9_out, and_10_out, and_11_out,
       and_12_out, and_13_out, and_14_out, and_15_out, and_16_out, and_17_out, and_18_out, and_19_out,
       and_20_out, and_21_out, and_22_out, and_23_out, and_24_out, and_25_out, and_26_out, and_27_out,
       and_28_out, and_29_out, and_30_out, and_31_out, and_32_out, not_1_out, not_2_out, not_3_out,
       not_4_out, not_5_out, not_6_out, not_7_out, not_8_out, not_9_out, not_10_out, not_11_out, not_12_out,
       not_13_out, not_14_out, not_15_out, not_16_out, not_17_out, not_18_out, not_19_out, not_20_out,
       not_21_out, not_22_out, not_23_out, not_24_out, not_25_out, not_26_out, not_27_out, not_28_out,
       not_29_out, not_30_out, not_31_out, not_32_out, not_33_out, not_34_out, not_35_out, not_36_out,
       not_37_out, not_38_out, not_39_out, not_40_out, not_41_out, not_42_out, not_43_out, not_44_out,
       not_45_out, not_46_out, not_47_out;

  not not_1 (not_1_out, opcode1);
  not not_2 (not_2_out, opcode2);
  not not_3 (not_3_out, opcode3);
  not not_4 (not_4_out, opcode4);
  not not_5 (not_5_out, opcode6);
  not not_6 (not_6_out, opcode1);
  not not_7 (not_7_out, opcode3);
  not not_8 (not_8_out, opcode4);
  not not_9 (not_9_out, opcode3);
  not not_10 (not_10_out, opcode4);
  not not_11 (not_11_out, opcode3);
  not not_12 (not_12_out, opcode4);
  not not_13 (not_13_out, opcode3);
  not not_14 (not_14_out, opcode4);
  not not_15 (not_15_out, opcode3);
  not not_16 (not_16_out, opcode4);
  not not_17 (not_17_out, opcode3);
  not not_18 (not_18_out, opcode4);
  not not_19 (not_19_out, opcode1);
  not not_20 (not_20_out, opcode1);
  not not_21 (not_21_out, opcode2);
  not not_22 (not_22_out, opcode4);
  not not_23 (not_23_out, opcode5);
  not not_24 (not_24_out, opcode1);
  not not_25 (not_25_out, opcode3);
  not not_26 (not_26_out, opcode5);
  not not_27 (not_27_out, opcode6);
  not not_28 (not_28_out, opcode6);
  not not_29 (not_29_out, opcode3);
  not not_30 (not_30_out, opcode4);
  not not_31 (not_31_out, opcode5);
  not not_32 (not_32_out, opcode6);
  not not_33 (not_33_out, opcode2);
  not not_34 (not_34_out, opcode6);
  not not_35 (not_35_out, opcode6);
  not not_36 (not_36_out, opcode4);
  not not_37 (not_37_out, opcode6);
  not not_38 (not_38_out, opcode3);
  not not_39 (not_39_out, opcode6);
  not not_40 (not_40_out, opcode3);
  not not_41 (not_41_out, opcode4);
  not not_42 (not_42_out, opcode5);
  not not_43 (not_43_out, opcode6);
  not not_44 (not_44_out, opcode5);
  not not_45 (not_45_out, opcode5);
  not not_46 (not_46_out, opcode5);
  not not_47 (not_47_out, opcode6);
  and and_1 (jump, not_1_out, not_2_out, not_3_out, not_4_out, opcode5, not_5_out);
  and and_2 (branch, not_6_out, opcode4);
  and and_3 (and_3_out, not_7_out, not_8_out, opcode5, opcode6);
  and and_4 (and_4_out, opcode2, not_9_out, not_10_out, opcode6);
  and and_5 (and_5_out, opcode1, not_11_out, not_12_out, opcode6);
  and and_6 (and_6_out, opcode1, opcode2, opcode3, opcode4, opcode5, opcode6);
  and and_7 (and_7_out, not_13_out, not_14_out, opcode5, opcode6);
  and and_8 (and_8_out, opcode2, not_15_out, not_16_out, opcode6);
  and and_9 (and_9_out, opcode1, not_17_out, not_18_out, opcode6);
  and and_10 (and_10_out, opcode1, opcode2, opcode3, opcode4, opcode5, opcode6);
  and and_11 (and_11_out, not_19_out, opcode5, opcode6);
  and and_12 (and_12_out, not_20_out, opcode4, opcode6);
  and and_13 (and_13_out, not_21_out, opcode3, opcode6);
  and and_14 (and_14_out, opcode3, not_22_out, opcode6);
  and and_15 (and_15_out, opcode3, not_23_out, opcode6);
  and and_16 (and_16_out, not_24_out, opcode2, opcode6);
  and and_17 (and_17_out, not_25_out, not_26_out, not_27_out);
  and and_18 (and_18_out, opcode4, opcode6);
  and and_19 (and_19_out, opcode3, opcode4);
  and and_20 (and_20_out, opcode1, not_28_out);
  and and_21 (and_21_out, not_29_out, not_30_out, not_31_out, not_32_out);
  and and_22 (and_22_out, not_33_out, opcode3, not_34_out);
  and and_23 (and_23_out, opcode3, opcode4, not_35_out);
  and and_24 (and_24_out, opcode2, not_36_out, opcode5, not_37_out);
  and and_25 (and_25_out, opcode1, not_38_out);
  and and_26 (and_26_out, opcode1, not_39_out);
  and and_27 (and_27_out, opcode1, opcode2, opcode4, opcode5);
  and and_28 (and_28_out, not_40_out, not_41_out, not_42_out, not_43_out);
  and and_29 (and_29_out, opcode4, not_44_out, opcode6);
  and and_30 (and_30_out, opcode3, not_45_out, opcode6);
  and and_31 (and_31_out, opcode1, not_46_out);
  and and_32 (and_32_out, opcode1, not_47_out);
  or or_1 (memread, and_3_out, and_4_out, and_5_out, and_6_out);
  or or_2 (memtoreg, and_7_out, and_8_out, and_9_out, and_10_out);
  or or_3 (memwrite, and_11_out, and_12_out, and_13_out, and_14_out, and_15_out, and_16_out);
  or or_4 (alusrc, and_17_out, and_18_out, and_19_out, opcode2, and_20_out);
  or or_5 (regwrite, and_21_out, and_22_out, and_23_out, and_24_out, and_25_out, and_26_out, and_27_out);
  or or_6 (regdst, and_28_out, and_29_out, and_30_out, opcode2, and_31_out, and_32_out);
endmodule
