// Logisim project RegFile.circ as structural Verilog: 1 circuit, main circuit main
module main (
  input  [15:0] Write_Data,
  input  RegWrite,
  input  [2:0] WriteAddr,
  input  [2:0] Read_Addr_1,
  input  CLK,
  input  Reset,
  input  [2:0] Read_Addr_2,
  output [15:0] Read_Data_1,
  output [15:0] Read_Data_2
);

  wire demultiplexer_1_out0, demultiplexer_1_out1, demultiplexer_1_out2, demultiplexer_1_out3,
       demultiplexer_1_out4, demultiplexer_1_out5, demultiplexer_1_out6, demultiplexer_1_out7;
  wire [15:0] _0_q, _1_q, _2_q, _3_q, _4_q, _5_q, _6_q, _7_q;

  Demultiplexer #(.select(3), .enable("false")) demultiplexer_1 (
    .out0(demultiplexer_1_out0), .out1(demultiplexer_1_out1), .out2(demultiplexer_1_out2),
    .out3(demultiplexer_1_out3), .out4(demultiplexer_1_out4), .out5(demultiplexer_1_out5),
    .out6(demultiplexer_1_out6), .out7(demultiplexer_1_out7), .in(RegWrite), .sel(WriteAddr));
  Register #(.width(16)) _0 (.D(Write_Data), .en(demultiplexer_1_out0), .Q(_0_q), .clk(CLK), .clr(Reset));
  Register #(.width(16)) _1 (.D(Write_Data), .en(demultiplexer_1_out1), .Q(_1_q), .clk(CLK), .clr(Reset));
  Register #(.width(16)) _2 (.D(Write_Data), .en(demultiplexer_1_out2), .Q(_2_q), .clk(CLK), .clr(Reset));
  Register #(.width(16)) _3 (.D(Write_Data), .en(demultiplexer_1_out3), .Q(_3_q), .clk(CLK), .clr(Reset));
  Register #(.width(16)) _4 (.D(Write_Data), .en(demultiplexer_1_out4), .Q(_4_q), .clk(CLK), .clr(Reset));
  Register #(.width(16)) _5 (.D(Write_Data), .en(demultiplexer_1_out5), .Q(_5_q), .clk(CLK), .clr(Reset));
  Register #(.width(16)) _6 (.D(Write_Data), .en(demultiplexer_1_out6), .Q(_6_q), .clk(CLK), .clr(Reset));
  Register #(.width(16)) _7 (.D(Write_Data), .en(demultiplexer_1_out7), .Q(_7_q), .clk(CLK), .clr(Reset));
  Multiplexer #(.select(3), .width(16)) multiplexer_1 (
    .in0(_0_q), .in1(_1_q), .in2(_2_q), .in3(_3_q), .in4(_4_q), .in5(_5_q), .in6(_6_q), .in7(_7_q),
    .out(Read_Data_1), .sel(Read_Addr_1), .en(1'b1));
  Multiplexer #(.select(3), .width(16)) multiplexer_2 (
    .in0(_0_q), .in1(_1_q), .in2(_2_q), .in3(_3_q), .in4(_4_q), .in5(_5_q), .in6(_6_q), .in7(_7_q),
    .out(Read_Data_2), .sel(Read_Addr_2), .en(1'b1));
endmodule
