// Logisim project datamemory.circ as structural Verilog: 1 circuit, main circuit main
module main (
  input  [15:0] Address,
  input  [15:0] Write_Data,
  input  CLR,
  input  MemRead,
  input  CLK,
  input  MemWrite,
  output [15:0] Read_Data
);

  RAM #(.addrWidth(16), .dataWidth(16), .bus("separate")) ram_1 (
    .addr(Address), .din(Write_Data), .data(Read_Data), .str(MemWrite), .clk(CLK), .ld(MemRead), .clr(CLR));  // open: sel
endmodule
