// Logisim project instructionmemory.circ as structural Verilog: 4 circuits, main circuit 32
module _26 (
  input  [25:0] Address,
  output [31:0] Instruction
);

  wire decoder_1_out0, decoder_1_out1, decoder_1_out2, decoder_1_out3;
  wire [31:0] rom_1_data, rom_2_data, rom_3_data, rom_4_data;

  Decoder #(.select(2), .enable("false")) decoder_1 (
    .out0(decoder_1_out0), .out1(decoder_1_out1), .out2(decoder_1_out2), .out3(decoder_1_out3),
    .sel(Address[25:24]));
  ROM #(.addrWidth(24), .dataWidth(32)) rom_1 (.addr(Address[23:0]), .data(rom_1_data), .sel(decoder_1_out0));
  ROM #(.addrWidth(24), .dataWidth(32)) rom_2 (.addr(Address[23:0]), .data(rom_2_data), .sel(decoder_1_out1));
  ROM #(.addrWidth(24), .dataWidth(32)) rom_3 (.addr(Address[23:0]), .data(rom_3_data), .sel(decoder_1_out2));
  ROM #(.addrWidth(24), .dataWidth(32)) rom_4 (.addr(Address[23:0]), .data(rom_4_data), .sel(decoder_1_out3));
  Multiplexer #(.select(2), .width(32), .enable("false")) multiplexer_1 (
    .in0(rom_1_data), .in1(rom_2_data), .in2(rom_3_data), .in3(rom_4_data), .out(Instruction),
    .sel(Address[25:24]));

  // Other names for the same wires on the sheet: MUX[1:0] = Address[25:24]
endmodule

module _28 (
  input  [27:0] Address,
  output [31:0] Out
);

  wire [31:0] n26_1_instruction, n26_2_instruction, n26_3_instruction, n26_4_instruction;

  _26 u_26_1 (.Address(Address[25:0]), .Instruction(n26_1_instruction));
  _26 u_26_2 (.Address(Address[25:0]), .Instruction(n26_2_instruction));
  _26 u_26_3 (.Address(Address[25:0]), .Instruction(n26_3_instruction));
  _26 u_26_4 (.Address(Address[25:0]), .Instruction(n26_4_instruction));
  Multiplexer #(.select(2), .width(32), .enable("false")) multiplexer_1 (
    .in0(n26_1_instruction), .in1(n26_2_instruction), .in2(n26_3_instruction), .in3(n26_4_instruction),
    .out(Out), .sel(Address[27:26]));

  // Other names for the same wires on the sheet: MUX[1:0] = Address[27:26]
endmodule

module _30 (
  input  [29:0] Address,
  output [31:0] Out
);

  wire [31:0] n28_1_out, n28_2_out, n28_3_out, n28_4_out;

  _28 u_28_1 (.Address(Address[27:0]), .Out(n28_1_out));
  _28 u_28_2 (.Address(Address[27:0]), .Out(n28_2_out));
  _28 u_28_3 (.Address(Address[27:0]), .Out(n28_3_out));
  _28 u_28_4 (.Address(Address[27:0]), .Out(n28_4_out));
  Multiplexer #(.select(2), .width(32), .enable("false")) multiplexer_1 (
    .in0(n28_1_out), .in1(n28_2_out), .in2(n28_3_out), .in3(n28_4_out), .out(Out), .sel(Address[29:28]));

  // Other names for the same wires on the sheet: MUX[1:0] = Address[29:28]
endmodule

module _32 (
  input  [31:0] Address,
  output [31:0] Out
);

  wire [31:0] n30_1_out, n30_2_out, n30_3_out, n30_4_out;

  _30 u_30_1 (.Address(Address[29:0]), .Out(n30_1_out));
  _30 u_30_2 (.Address(Address[29:0]), .Out(n30_2_out));
  _30 u_30_3 (.Address(Address[29:0]), .Out(n30_3_out));
  _30 u_30_4 (.Address(Address[29:0]), .Out(n30_4_out));
  Multiplexer #(.select(2), .width(32), .enable("false")) multiplexer_1 (
    .in0(n30_1_out), .in1(n30_2_out), .in2(n30_3_out), .in3(n30_4_out), .out(Out), .sel(Address[31:30]));

  // Other names for the same wires on the sheet: MUX[1:0] = Address[31:30]
endmodule
